// Logisim project real alu.circ as structural Verilog
module in_A_AND_in_b (
  input  [7:0] A,
  input  [7:0] b,
  output [7:0] out_3
);

  assign out_3 = A & b;  // AND_Gate and_1, 8 bits wide
endmodule

module in_A_OR_in_b (
  input  [7:0] A,
  input  [7:0] b,
  output [7:0] out_3
);

  assign out_3 = A | b;  // OR_Gate or_1, 8 bits wide
endmodule

module NOT_in_b (
  input  [7:0] in_1,
  output [7:0] out_2
);

  assign out_2 = ~in_1;  // NOT_Gate not_1, 8 bits wide
endmodule

module LSL_in_b (
  input  [7:0] in_1,
  output [7:0] out_2,
  output overflow
);


  assign out_2 = {in_1[6:0], 1'b0};
  assign overflow = in_1[7];
endmodule

module LSR_in_b (
  input  [7:0] in_1,
  output out_2,
  output [7:0] out_3
);


  assign out_2 = in_1[0];
  assign out_3 = {1'b0, in_1[7:1]};
endmodule

module gf (
);

  LSR_in_b lsr_in_b_1 ();  // open: in_1, out_2, out_3
  NOT_in_b not_in_b_1 ();  // open: in_1, out_2
endmodule
